# Fritzing sketch DHT11 (saved by Fritzing 0.9.7b)

parts:
  Mod1 = Raspberry Pi 4B
  DHT1 = DHT11 Humitidy and Temperature Sensor

nets:
  3V3: Mod1.3V3, DHT1.VDD
  GND: Mod1.GND, DHT1.GND
  N1: Mod1.GPIO14, DHT1.DATA

custom parts:
  DHT11 Humitidy and Temperature Sensor: DHT11 Humidity and Temperature Sensor
