# Fritzing sketch DS18B20 (saved by Fritzing 0.9.7b)
breadboards: 1

parts:
  Mod1 = Raspberry Pi 4B
  DS1 = DS18B20 1-Wire Temperature Sensor [part_number=DS18B20]
  R1 = Resistor [tolerance=±5% power=0.25 resistance=4.7k package=THT]
  J1 = screw terminal, 6 pins

nets:
  3V3: Mod1.3V3, DS1.VDD, R1.Pin_0, J1.pin3, J1.pin6
  GND: Mod1.GND, DS1.GND, J1.pin1
  N1: Mod1.GPIO4, DS1.DQ, R1.Pin_1, J1.pin2
